# Fritzing sketch AlarmBoard (saved by Fritzing 0.9.3b)
circuit board: 8.46667cm x 5.64444cm
breadboards: 1

parts:
  Raspberry_Pi_Zero1 = Raspberry Pi Zero
  LED1 = RGB LED (com. cathode, rgb) [package="5 mm [THT]"]
  R1 = Resistor [tolerance=±5% resistance=220 package=THT]
  R2 = Resistor [tolerance=±5% resistance=220 package=THT]
  R3 = Resistor [tolerance=±5% resistance=220 package=THT]
  Componente1 = Taiway 100-SP-X-T1 SPDT Miniature Toggle Switch [part_number=100-SP-X-T1-0-0-B1-M1 package=THT]  # not connected

nets:
  N1: Raspberry_Pi_Zero1.GND, LED1.common_cathode
  N2: Raspberry_Pi_Zero1.GPIO21, R3.Pin_1
  N3: Raspberry_Pi_Zero1.GPIO20, R2.Pin_1
  N4: Raspberry_Pi_Zero1.GPIO16, R1.Pin_1
  N5: LED1.red_anode, R1.Pin_0
  N6: LED1.green_anode, R2.Pin_0
  N7: LED1.blue_anode, R3.Pin_0
